# Fritzing sketch Diagram (saved by Fritzing 0.8.7b)

parts:
  Part1 = Arduino Nano (Rev3.0)  # not connected
  S1 = Pushbutton [package=THT]
  J1 = female pin header, 2 pins [form="♀ (female)"]

nets:
  N1: S1.leg0, J1.pin2
  N2: S1.leg1, J1.pin1
